// Logisim project 22bit-computer.circ as structural Verilog: 28 circuits, main circuit 4bit CLA
// CLA
module _4bit_CLA (
  input  Cin,
  input  [3:0] A,
  input  [3:0] B,
  output [3:0] S,
  output Cout
);

  wire and_1_out, and_2_out, and_3_out, and_4_out, and_5_out, and_6_out, and_7_out, and_8_out, and_9_out,
       and_10_out, C1_out, C2_out, C3_out, G1_out, G2_out, G3_out, G4_out, P1_out, P2_out, P3_out, P4_out;

  xor P1 (P1_out, A[0], B[0]);
  and G1 (G1_out, A[0], B[0]);
  xor P2 (P2_out, A[1], B[1]);
  and G2 (G2_out, A[1], B[1]);
  xor P3 (P3_out, A[2], B[2]);
  and G3 (G3_out, A[2], B[2]);
  xor P4 (P4_out, A[3], B[3]);
  and G4 (G4_out, A[3], B[3]);
  and and_1 (and_1_out, Cin, P1_out);
  and and_2 (and_2_out, G1_out, P2_out);
  and and_3 (and_3_out, G2_out, P3_out);
  and and_4 (and_4_out, G1_out, P2_out, P3_out);
  and and_5 (and_5_out, P3_out, P2_out, P1_out, Cin);
  and and_6 (and_6_out, P1_out, P4_out, Cin, P2_out, P3_out);
  and and_7 (and_7_out, P4_out, P2_out, P3_out, G1_out);
  and and_8 (and_8_out, P4_out, P3_out, G2_out);
  and and_9 (and_9_out, G3_out, P4_out);
  or C1 (C1_out, and_1_out, G1_out);
  and and_10 (and_10_out, Cin, P1_out, P2_out);
  or C3 (C3_out, and_3_out, and_4_out, G3_out, and_5_out);
  xor S1 (S[0], Cin, P1_out);
  xor S2 (S[1], C1_out, P2_out);
  or C2 (C2_out, and_2_out, G2_out, and_10_out);
  or u_Cout (Cout, and_6_out, and_7_out, and_8_out, and_9_out, G4_out);
  xor S3 (S[2], C2_out, P3_out);
  xor S4 (S[3], C3_out, P4_out);

  // Notes on the sheet:
  //   2207035
  //    4 bit CLA
endmodule

// CLA
module _2bit_CLA (
  input  Cin,
  input  [1:0] A,
  input  [1:0] B,
  output [1:0] S,
  output Cout
);

  wire and_1_out, and_2_out, and_3_out, C1_out, G1_out, G2_out, P1_out, P2_out;

  xor P1 (P1_out, A[0], B[0]);
  and G1 (G1_out, A[0], B[0]);
  xor P2 (P2_out, A[1], B[1]);
  and G2 (G2_out, A[1], B[1]);
  and and_1 (and_1_out, Cin, P1_out);
  and and_2 (and_2_out, G1_out, P2_out);
  and and_3 (and_3_out, P2_out, P1_out, Cin);
  or C1 (C1_out, and_1_out, G1_out);
  or C2 (Cout, and_2_out, and_3_out, G2_out);
  xor S1 (S[0], Cin, P1_out);
  xor S2 (S[1], P2_out, C1_out);

  // Notes on the sheet:
  //   2207035
  //   2 bit CLA
endmodule

// Adder
module _22bit_Adder (
  input  Control__0_Add___1_Sub,
  input  [21:0] A,
  input  [21:0] B,
  output [21:0] Result,
  output Carry_Out,
  output Overflow
);

  wire and_1_out, and_2_out, n4bit_adder_sub_1_cout, n4bit_adder_sub_2_cout, n4bit_adder_sub_3_cout,
       n4bit_adder_sub_4_cout, n4bit_adder_sub_5_cout, not_1_out, not_2_out, not_3_out;

  _4bit_Adder_Sub u_4bit_adder_sub_1 (
    .A(A[3:0]), .B(B[3:0]), .Control(Control__0_Add___1_Sub), .Cin(Control__0_Add___1_Sub),
    .Cout(n4bit_adder_sub_1_cout), .Result(Result[3:0]));
  _4bit_Adder_Sub u_4bit_adder_sub_2 (
    .A(A[7:4]), .B(B[7:4]), .Control(Control__0_Add___1_Sub), .Cin(n4bit_adder_sub_1_cout),
    .Cout(n4bit_adder_sub_2_cout), .Result(Result[7:4]));
  _4bit_Adder_Sub u_4bit_adder_sub_3 (
    .A(A[11:8]), .B(B[11:8]), .Control(Control__0_Add___1_Sub), .Cin(n4bit_adder_sub_2_cout),
    .Cout(n4bit_adder_sub_3_cout), .Result(Result[11:8]));
  _4bit_Adder_Sub u_4bit_adder_sub_4 (
    .A(A[15:12]), .B(B[15:12]), .Control(Control__0_Add___1_Sub), .Cin(n4bit_adder_sub_3_cout),
    .Cout(n4bit_adder_sub_4_cout), .Result(Result[15:12]));
  _4bit_Adder_Sub u_4bit_adder_sub_5 (
    .A(A[19:16]), .B(B[19:16]), .Control(Control__0_Add___1_Sub), .Cin(n4bit_adder_sub_4_cout),
    .Cout(n4bit_adder_sub_5_cout), .Result(Result[19:16]));
  _2bit_adder_sub u_2bit_adder_sub_1 (
    .A(A[21:20]), .B(B[21:20]), .Control(Control__0_Add___1_Sub), .Cin(n4bit_adder_sub_5_cout),
    .Cout(Carry_Out), .Result(Result[21:20]));
  not not_1 (not_1_out, Result[21]);
  not not_2 (not_2_out, A[21]);
  not not_3 (not_3_out, B[21]);
  and and_1 (and_1_out, not_1_out, A[21], B[21]);
  and and_2 (and_2_out, Result[21], not_2_out, not_3_out);
  or or_1 (Overflow, and_1_out, and_2_out);

  // Notes on the sheet:
  //   2207035
  //   22 bit Adder
endmodule

// AND
module _22bit_AND (
  input  [21:0] A,
  input  [21:0] B,
  output [21:0] A___B
);

  assign A___B = A & B;  // AND_Gate and_1, 22 bits wide

  // Notes on the sheet:
  //   2207035
  //   22 bit AND
endmodule

// OR
module _22bit_OR (
  input  [21:0] A,
  input  [21:0] B,
  output [21:0] A___B
);

  assign A___B = A | B;  // OR_Gate or_1, 22 bits wide

  // Notes on the sheet:
  //   2207035
  //   22 bit OR
endmodule

// Neg
module _22bit_Negative_Check (
  input  [21:0] Input,
  output out_2
);


  assign out_2 = Input[21];

  // Notes on the sheet:
  //   2207035
  //   22 bit Negative Check
endmodule

// Zero
module _22bit_zero_check (
  input  [21:0] Input,
  output output__zero_0
);

  or or_1 (output__zero_0, Input[0], Input[1], Input[2], Input[3], Input[4], Input[5], Input[6], Input[7], Input[8], Input[9], Input[10], Input[11], Input[12], Input[13], Input[14], Input[15], Input[16], Input[17], Input[18], Input[19], Input[20], Input[21]);

  // Notes on the sheet:
  //   2207035
  //   22 bit Zero Check
endmodule

module _4bit_Adder_Sub (
  input  Control,
  input  Cin,
  input  [3:0] A,
  input  [3:0] B,
  output [3:0] Result,
  output Cout
);

  wire [3:0] xor_1_out;

  xor xor_1 (xor_1_out[0], Control, B[0]);
  xor xor_2 (xor_1_out[1], Control, B[1]);
  xor xor_3 (xor_1_out[2], Control, B[2]);
  xor xor_4 (xor_1_out[3], Control, B[3]);
  _4bit_CLA u_4bit_cla_1 (.A(A), .B(xor_1_out), .Cin(Cin), .Cout(Cout), .S(Result));

  // Notes on the sheet:
  //   2207035
  //   4 bit adder or Subtractor
endmodule

module _2bit_adder_sub (
  input  Control,
  input  Cin,
  input  [1:0] A,
  input  [1:0] B,
  output [1:0] Result,
  output Cout
);

  wire [1:0] xor_1_out;

  xor xor_1 (xor_1_out[0], Control, B[0]);
  xor xor_2 (xor_1_out[1], Control, B[1]);
  _2bit_CLA u_2bit_cla_1 (.A(A), .B(xor_1_out), .Cin(Cin), .Cout(Cout), .S(Result));

  // Notes on the sheet:
  //   2207035
  //   2 bit adder or Subtractor
endmodule

// Counter
module counter (
  input  [1:0] Q,
  input  [2:0] T,
  input  C,
  output DA,
  output DB,
  output DC
);

  wire and_1_out, and_2_out, and_3_out, and_4_out, and_5_out, or_1_out, or_2_out, Q0, Q1, Q2, Q3, T0, T1, T2,
       T3, T4, T5, T6, T7;

  Decoder #(.select(2), .enable("false")) decoder_1 (.out0(Q0), .out1(Q1), .out2(Q2), .out3(Q3), .sel(Q));
  Decoder #(.select(3), .enable("false")) decoder_2 (
    .out0(T0), .out1(T1), .out2(T2), .out3(T3), .out4(T4), .out5(T5), .out6(T6), .out7(T7), .sel(T));
  or or_1 (or_1_out, Q0, Q2, Q3);
  or or_2 (or_2_out, Q0, Q1, Q3);
  and and_1 (and_1_out, T2, or_1_out);
  and and_2 (and_2_out, T6, C);
  and and_3 (and_3_out, T2, Q2);
  and and_4 (and_4_out, T2, or_2_out);
  and and_5 (and_5_out, T6, C);
  or or_3 (DA, T0, and_1_out, T3, T4, and_2_out, T7);
  or or_4 (DB, T1, and_3_out, T5, T6, T6, T7);
  or or_5 (DC, T5, and_4_out, T3, T4, and_5_out, T7);

  // Notes on the sheet:
  //   2207035
  //   Counter
endmodule

module Sequence_Detector (
  input  clk,
  input  reset,
  input  Q0,
  input  Q_1,
  input  [4:0] count,
  output CL__A__Q_1,
  output Load__M__Q__Cnt,
  output Load_A,
  output C0,
  output C1,
  output Shr,
  output Dec_Cnt
);

  wire counter_1_da, counter_1_db, counter_1_dc, nor_1_out, T0, T2, T4, T6, T7;
  wire [2:0] T;

  nor nor_1 (nor_1_out, count[0], count[1], count[2], count[3], count[4]);
  counter counter_1 (.Q({Q0, Q_1}), .T(T), .C(nor_1_out), .DA(counter_1_da), .DB(counter_1_db), .DC(counter_1_dc));
  Decoder #(.select(3), .enable("false")) decoder_1 (
    .out0(T0), .out1(CL__A__Q_1), .out2(T2), .out3(C0), .out4(T4), .out5(Dec_Cnt), .out6(T6), .out7(T7),
    .sel(T));
  D_Flip_Flop d_ff_1 (.clk(clk), .D(counter_1_da), .Q(T[0]), .reset(reset));  // open: Qn, preset, en
  D_Flip_Flop d_ff_2 (.clk(clk), .D(counter_1_db), .Q(T[1]), .reset(reset));  // open: Qn, preset, en
  D_Flip_Flop d_ff_3 (.clk(clk), .D(counter_1_dc), .Q(T[2]), .reset(reset));  // open: Qn, preset, en
  or or_1 (Load_A, C0, T4);
  or or_2 (C1, T4, C0);

  assign Load__M__Q__Cnt = CL__A__Q_1;
  assign Shr = Dec_Cnt;

  // Other names for the same wires on the sheet: T1 = CL__A__Q_1; T3 = C0; T5 = Dec_Cnt

  // Notes on the sheet:
  //   2207035
  //   Sequence Detector
endmodule

module _22bit_booths_multiplier (
  input  [21:0] in_1,
  input  [21:0] in_2,
  output [21:0] out_3,
  output [21:0] out_4
);

  wire Clk_out, or_1_out, Reset_out, sequence_detector_1_cl__a__q_1, sequence_detector_1_dec_cnt,
       sequence_detector_1_load__m__q__cnt, sequence_detector_1_load_a, sequence_detector_1_shr,
       shift_register_1_out, shift_register_3_out, shift_register_4_q0;
  wire [1:0] sequence_detector_1_c0;
  wire [4:0] counter_1_q;
  wire [21:0] n22bit_alu_1_output, shift_register_2_q21;

  Button Reset (.out(Reset_out));
  Clock Clk (.out(Clk_out));
  Sequence_Detector sequence_detector_1 (
    .clk(Clk_out), .reset(Reset_out), .Q0(out_4[0]), .Q_1(shift_register_4_q0), .count(counter_1_q),
    .CL__A__Q_1(sequence_detector_1_cl__a__q_1), .Load__M__Q__Cnt(sequence_detector_1_load__m__q__cnt),
    .Load_A(sequence_detector_1_load_a), .C0(sequence_detector_1_c0[0]), .C1(sequence_detector_1_c0[1]),
    .Shr(sequence_detector_1_shr), .Dec_Cnt(sequence_detector_1_dec_cnt));
  or or_1 (or_1_out, sequence_detector_1_dec_cnt, sequence_detector_1_load__m__q__cnt);
  Counter #(.width(5), .max('h16)) counter_1 (
    .load(or_1_out), .D(5'b10110), .count(sequence_detector_1_dec_cnt), .Q(counter_1_q), .clk(Clk_out));  // open: carry, clr
  Shift_Register #(.length(22)) shift_register_1 (
    .shift(sequence_detector_1_shr), .in(out_3[21]), .clk(Clk_out), .out(shift_register_1_out),
    .load(sequence_detector_1_load_a), .clr(sequence_detector_1_cl__a__q_1), .d0(n22bit_alu_1_output[21]),
    .q0(out_3[21]), .d1(n22bit_alu_1_output[20]), .q1(out_3[20]), .d2(n22bit_alu_1_output[19]),
    .q2(out_3[19]), .d3(n22bit_alu_1_output[18]), .q3(out_3[18]), .d4(n22bit_alu_1_output[17]),
    .q4(out_3[17]), .d5(n22bit_alu_1_output[16]), .q5(out_3[16]), .d6(n22bit_alu_1_output[15]),
    .q6(out_3[15]), .d7(n22bit_alu_1_output[14]), .q7(out_3[14]), .d8(n22bit_alu_1_output[13]),
    .q8(out_3[13]), .d9(n22bit_alu_1_output[12]), .q9(out_3[12]), .d10(n22bit_alu_1_output[11]),
    .q10(out_3[11]), .d11(n22bit_alu_1_output[10]), .q11(out_3[10]), .d12(n22bit_alu_1_output[9]),
    .q12(out_3[9]), .d13(n22bit_alu_1_output[8]), .q13(out_3[8]), .d14(n22bit_alu_1_output[7]),
    .q14(out_3[7]), .d15(n22bit_alu_1_output[6]), .q15(out_3[6]), .d16(n22bit_alu_1_output[5]),
    .q16(out_3[5]), .d17(n22bit_alu_1_output[4]), .q17(out_3[4]), .d18(n22bit_alu_1_output[3]),
    .q18(out_3[3]), .d19(n22bit_alu_1_output[2]), .q19(out_3[2]), .d20(n22bit_alu_1_output[1]),
    .q20(out_3[1]), .d21(n22bit_alu_1_output[0]), .q21(out_3[0]));
  Shift_Register #(.length(22)) shift_register_2 (
    .shift(1'b0), .clk(Clk_out), .load(sequence_detector_1_load__m__q__cnt), .d0(in_1[21]),
    .q0(shift_register_2_q21[21]), .d1(in_1[20]), .q1(shift_register_2_q21[20]), .d2(in_1[19]),
    .q2(shift_register_2_q21[19]), .d3(in_1[18]), .q3(shift_register_2_q21[18]), .d4(in_1[17]),
    .q4(shift_register_2_q21[17]), .d5(in_1[16]), .q5(shift_register_2_q21[16]), .d6(in_1[15]),
    .q6(shift_register_2_q21[15]), .d7(in_1[14]), .q7(shift_register_2_q21[14]), .d8(in_1[13]),
    .q8(shift_register_2_q21[13]), .d9(in_1[12]), .q9(shift_register_2_q21[12]), .d10(in_1[11]),
    .q10(shift_register_2_q21[11]), .d11(in_1[10]), .q11(shift_register_2_q21[10]), .d12(in_1[9]),
    .q12(shift_register_2_q21[9]), .d13(in_1[8]), .q13(shift_register_2_q21[8]), .d14(in_1[7]),
    .q14(shift_register_2_q21[7]), .d15(in_1[6]), .q15(shift_register_2_q21[6]), .d16(in_1[5]),
    .q16(shift_register_2_q21[5]), .d17(in_1[4]), .q17(shift_register_2_q21[4]), .d18(in_1[3]),
    .q18(shift_register_2_q21[3]), .d19(in_1[2]), .q19(shift_register_2_q21[2]), .d20(in_1[1]),
    .q20(shift_register_2_q21[1]), .d21(in_1[0]), .q21(shift_register_2_q21[0]));  // open: in, out, clr
  Shift_Register #(.length(22)) shift_register_3 (
    .shift(sequence_detector_1_shr), .in(shift_register_1_out), .clk(Clk_out), .out(shift_register_3_out),
    .load(sequence_detector_1_load__m__q__cnt), .d0(in_2[21]), .q0(out_4[21]), .d1(in_2[20]), .q1(out_4[20]),
    .d2(in_2[19]), .q2(out_4[19]), .d3(in_2[18]), .q3(out_4[18]), .d4(in_2[17]), .q4(out_4[17]),
    .d5(in_2[16]), .q5(out_4[16]), .d6(in_2[15]), .q6(out_4[15]), .d7(in_2[14]), .q7(out_4[14]),
    .d8(in_2[13]), .q8(out_4[13]), .d9(in_2[12]), .q9(out_4[12]), .d10(in_2[11]), .q10(out_4[11]),
    .d11(in_2[10]), .q11(out_4[10]), .d12(in_2[9]), .q12(out_4[9]), .d13(in_2[8]), .q13(out_4[8]),
    .d14(in_2[7]), .q14(out_4[7]), .d15(in_2[6]), .q15(out_4[6]), .d16(in_2[5]), .q16(out_4[5]),
    .d17(in_2[4]), .q17(out_4[4]), .d18(in_2[3]), .q18(out_4[3]), .d19(in_2[2]), .q19(out_4[2]),
    .d20(in_2[1]), .q20(out_4[1]), .d21(in_2[0]), .q21(out_4[0]));  // open: clr
  Shift_Register #(.length(1)) shift_register_4 (
    .shift(sequence_detector_1_shr), .in(shift_register_3_out), .clk(Clk_out),
    .clr(sequence_detector_1_cl__a__q_1), .q0(shift_register_4_q0));  // open: out, load, d0
  _22bit_ALU u_22bit_alu_1 (
    .Control(sequence_detector_1_c0), .A(out_3), .B(shift_register_2_q21), .\output (n22bit_alu_1_output));  // open: Negative_Zero_CarryOut_Overflow

  // Notes on the sheet:
  //   M
  //   Q
  //   2207035
  //   22 bit booths multiplier
  //   A
  //   Q
  //   22bit ALU
  //   Q-1
  //   Product
endmodule

// ALU
module _22bit_ALU (
  input  [1:0] Control,
  input  [21:0] A,
  input  [21:0] B,
  output [21:0] \output ,
  output [3:0] Negative_Zero_CarryOut_Overflow
);

  wire n22bit_zero_check_1_output__zero_0;
  wire [21:0] n22bit_adder_1_result, n22bit_and_1_a___b, n22bit_or_1_a___b;

  _22bit_AND u_22bit_and_1 (.A(A), .B(B), .A___B(n22bit_and_1_a___b));
  _22bit_OR u_22bit_or_1 (.A(B), .B(A), .A___B(n22bit_or_1_a___b));
  _22bit_Adder u_22bit_adder_1 (
    .A(A), .B(B), .Control__0_Add___1_Sub(Control[0]), .Result(n22bit_adder_1_result),
    .Carry_Out(Negative_Zero_CarryOut_Overflow[1]), .Overflow(Negative_Zero_CarryOut_Overflow[0]));
  Multiplexer #(.select(2), .width(22), .enable("false")) multiplexer_1 (
    .in0(n22bit_or_1_a___b), .in1(n22bit_and_1_a___b), .in2(n22bit_adder_1_result),
    .in3(n22bit_adder_1_result), .out(\output ), .sel(Control));
  _22bit_Negative_Check u_22bit_negative_check_1 (.Input(\output ), .out_2(Negative_Zero_CarryOut_Overflow[3]));
  not not_1 (Negative_Zero_CarryOut_Overflow[2], n22bit_zero_check_1_output__zero_0);
  _22bit_zero_check u_22bit_zero_check_1 (.Input(\output ), .output__zero_0(n22bit_zero_check_1_output__zero_0));

  // Notes on the sheet:
  //   00 - OR
  //   01 - AND
  //   10 - Adder
  //   11 - Subtractor
  //   Input
  //   2207035
  //   22 bit ALU
  //   FLAGS
endmodule

// PLR
module _4bit_PLR (
  input  LOAD,
  input  [3:0] in_2,
  input  CLK,
  input  CLR,
  output [3:0] out_5
);

  wire and_1_out, and_2_out, and_3_out, and_4_out, and_5_out, and_6_out, and_7_out, and_8_out, not_1_out,
       not_2_out, not_3_out, not_4_out;

  not not_1 (not_1_out, in_2[0]);
  not not_2 (not_2_out, in_2[1]);
  not not_3 (not_3_out, in_2[2]);
  not not_4 (not_4_out, in_2[3]);
  and and_1 (and_1_out, in_2[0], LOAD);
  and and_2 (and_2_out, not_1_out, LOAD);
  and and_3 (and_3_out, in_2[1], LOAD);
  and and_4 (and_4_out, not_2_out, LOAD);
  and and_5 (and_5_out, in_2[2], LOAD);
  and and_6 (and_6_out, not_3_out, LOAD);
  and and_7 (and_7_out, in_2[3], LOAD);
  and and_8 (and_8_out, not_4_out, LOAD);
  J_K_Flip_Flop j_k_ff_1 (.J(and_1_out), .clk(CLK), .K(and_2_out), .Q(out_5[0]), .reset(CLR));  // open: Qn, preset, en
  J_K_Flip_Flop j_k_ff_2 (.J(and_3_out), .clk(CLK), .K(and_4_out), .Q(out_5[1]), .reset(CLR));  // open: Qn, preset, en
  J_K_Flip_Flop j_k_ff_3 (.J(and_5_out), .clk(CLK), .K(and_6_out), .Q(out_5[2]), .reset(CLR));  // open: Qn, preset, en
  J_K_Flip_Flop j_k_ff_4 (.J(and_7_out), .clk(CLK), .K(and_8_out), .Q(out_5[3]), .reset(CLR));  // open: Qn, preset, en

  // Notes on the sheet:
  //   2207035
  //    4 bit PLR
endmodule

// PLR
module _2bit_PLR (
  input  LOAD,
  input  [1:0] in_2,
  input  CLK,
  input  CLR,
  output [1:0] out_5
);

  wire and_1_out, and_2_out, and_3_out, and_4_out, not_1_out, not_2_out;

  not not_1 (not_1_out, in_2[0]);
  not not_2 (not_2_out, in_2[1]);
  and and_1 (and_1_out, in_2[0], LOAD);
  and and_2 (and_2_out, not_1_out, LOAD);
  and and_3 (and_3_out, in_2[1], LOAD);
  and and_4 (and_4_out, not_2_out, LOAD);
  J_K_Flip_Flop j_k_ff_1 (.J(and_1_out), .clk(CLK), .K(and_2_out), .Q(out_5[0]), .reset(CLR));  // open: Qn, preset, en
  J_K_Flip_Flop j_k_ff_2 (.J(and_3_out), .clk(CLK), .K(and_4_out), .Q(out_5[1]), .reset(CLR));  // open: Qn, preset, en

  // Notes on the sheet:
  //   2207035
  //    2 bit PLR
endmodule

module _22bit_PLR (
  input  load,
  input  [21:0] in_2,
  input  in_3,
  output [21:0] out_4
);

  wire CLK_out;

  Clock CLK (.out(CLK_out));
  _4bit_PLR u_4bit_plr_1 (.in_2(in_2[3:0]), .CLK(CLK_out), .CLR(in_3), .LOAD(load), .out_5(out_4[3:0]));
  _4bit_PLR u_4bit_plr_2 (.in_2(in_2[7:4]), .CLK(CLK_out), .CLR(in_3), .LOAD(load), .out_5(out_4[7:4]));
  _4bit_PLR u_4bit_plr_3 (.in_2(in_2[11:8]), .CLK(CLK_out), .CLR(in_3), .LOAD(load), .out_5(out_4[11:8]));
  _4bit_PLR u_4bit_plr_4 (.in_2(in_2[15:12]), .CLK(CLK_out), .CLR(in_3), .LOAD(load), .out_5(out_4[15:12]));
  _4bit_PLR u_4bit_plr_5 (.in_2(in_2[19:16]), .CLK(CLK_out), .CLR(in_3), .LOAD(load), .out_5(out_4[19:16]));
  _2bit_PLR u_2bit_plr_1 (.in_2(in_2[21:20]), .CLK(CLK_out), .CLR(in_3), .LOAD(load), .out_5(out_4[21:20]));

  // Notes on the sheet:
  //   2207035
  //    22 bit PLR
endmodule

// CPL
module _4bit_CPL (
  input  Cin,
  input  count,
  input  load,
  input  [3:0] in_4,
  input  clk,
  input  clr,
  output [3:0] out_7,
  output Cout
);

  wire and_1_out, and_2_out, and_3_out, and_4_out, and_5_out, and_6_out, and_7_out, and_8_out, and_9_out,
       and_10_out, and_11_out, and_12_out, and_13_out, not_1_out, not_2_out, not_3_out, not_4_out, not_5_out,
       or_1_out, or_2_out, or_3_out, or_4_out, or_5_out, or_6_out, or_7_out, or_8_out;

  and and_1 (and_1_out, count, not_1_out);
  not not_1 (not_1_out, load);
  not not_2 (not_2_out, in_4[0]);
  not not_3 (not_3_out, in_4[1]);
  not not_4 (not_4_out, in_4[2]);
  not not_5 (not_5_out, in_4[3]);
  and and_2 (and_2_out, load, in_4[0]);
  and and_3 (and_3_out, load, not_2_out);
  and and_4 (and_4_out, load, in_4[1]);
  and and_5 (and_5_out, load, not_3_out);
  and and_6 (and_6_out, load, in_4[2]);
  and and_7 (and_7_out, load, not_4_out);
  and and_8 (and_8_out, load, in_4[3]);
  and and_9 (and_9_out, load, not_5_out);
  and and_10 (and_10_out, and_1_out, Cin);
  and and_11 (and_11_out, and_1_out, Cin, out_7[0]);
  and and_12 (and_12_out, out_7[0], Cin, out_7[1], and_1_out);
  and and_13 (and_13_out, and_1_out, out_7[0], Cin, out_7[1], out_7[2]);
  or or_1 (or_1_out, and_2_out, and_10_out);
  or or_2 (or_2_out, and_10_out, and_3_out);
  or or_3 (or_3_out, and_4_out, and_11_out);
  or or_4 (or_4_out, and_11_out, and_5_out);
  or or_5 (or_5_out, and_6_out, and_12_out);
  or or_6 (or_6_out, and_12_out, and_7_out);
  or or_7 (or_7_out, and_8_out, and_13_out);
  or or_8 (or_8_out, and_13_out, and_9_out);
  J_K_Flip_Flop j_k_ff_1 (.J(or_1_out), .clk(clk), .K(or_2_out), .Q(out_7[0]), .reset(clr));  // open: Qn, preset, en
  J_K_Flip_Flop j_k_ff_2 (.J(or_3_out), .clk(clk), .K(or_4_out), .Q(out_7[1]), .reset(clr));  // open: Qn, preset, en
  J_K_Flip_Flop j_k_ff_3 (.J(or_5_out), .clk(clk), .K(or_6_out), .Q(out_7[2]), .reset(clr));  // open: Qn, preset, en
  J_K_Flip_Flop j_k_ff_4 (.J(or_7_out), .clk(clk), .K(or_8_out), .Q(out_7[3]), .reset(clr));  // open: Qn, preset, en
  and and_14 (Cout, out_7[2], out_7[0], out_7[1], out_7[3], and_1_out, Cin);
  // Probe on out_7

  // Notes on the sheet:
  //   2207035
  //   4 bit CPL
endmodule

// CPL
module _2bit_CPL (
  input  Cin,
  input  count,
  input  LOAD,
  input  [1:0] in_4,
  input  CLR,
  input  CLK,
  output [1:0] out_7
);

  wire and_1_out, and_2_out, and_3_out, and_4_out, and_5_out, and_6_out, and_7_out, not_1_out, not_2_out,
       not_3_out, or_1_out, or_2_out, or_3_out, or_4_out;

  and and_1 (and_1_out, count, not_1_out);
  not not_1 (not_1_out, LOAD);
  not not_2 (not_2_out, in_4[0]);
  not not_3 (not_3_out, in_4[1]);
  and and_2 (and_2_out, LOAD, in_4[0]);
  and and_3 (and_3_out, LOAD, not_2_out);
  and and_4 (and_4_out, LOAD, in_4[1]);
  and and_5 (and_5_out, LOAD, not_3_out);
  and and_6 (and_6_out, and_1_out, Cin);
  and and_7 (and_7_out, and_1_out, Cin, out_7[0]);
  or or_1 (or_1_out, and_2_out, and_6_out);
  or or_2 (or_2_out, and_6_out, and_3_out);
  or or_3 (or_3_out, and_4_out, and_7_out);
  or or_4 (or_4_out, and_7_out, and_5_out);
  J_K_Flip_Flop j_k_ff_1 (.J(or_1_out), .clk(CLK), .K(or_2_out), .Q(out_7[0]), .reset(CLR));  // open: Qn, preset, en
  J_K_Flip_Flop j_k_ff_2 (.J(or_3_out), .clk(CLK), .K(or_4_out), .Q(out_7[1]), .reset(CLR));  // open: Qn, preset, en

  // Notes on the sheet:
  //   2207035
  //   2 bit CPL
endmodule

module _22bit_CPL (
  input  lOAD,
  input  Count,
  input  [21:0] in_3,
  input  CLR,
  output [21:0] out_5
);

  wire CLK_out, n4bit_cpl_1_cout, n4bit_cpl_2_cout, n4bit_cpl_3_cout, n4bit_cpl_4_cout, n4bit_cpl_5_cout;

  Clock CLK (.out(CLK_out));
  _4bit_CPL u_4bit_cpl_1 (
    .Cin(Count), .count(Count), .load(lOAD), .in_4(in_3[3:0]), .clk(CLK_out), .clr(CLR), .out_7(out_5[3:0]),
    .Cout(n4bit_cpl_1_cout));
  _4bit_CPL u_4bit_cpl_2 (
    .Cin(n4bit_cpl_1_cout), .count(Count), .load(lOAD), .in_4(in_3[7:4]), .clk(CLK_out), .clr(CLR),
    .out_7(out_5[7:4]), .Cout(n4bit_cpl_2_cout));
  _4bit_CPL u_4bit_cpl_3 (
    .Cin(n4bit_cpl_2_cout), .count(Count), .load(lOAD), .in_4(in_3[11:8]), .clk(CLK_out), .clr(CLR),
    .out_7(out_5[11:8]), .Cout(n4bit_cpl_3_cout));
  _4bit_CPL u_4bit_cpl_4 (
    .Cin(n4bit_cpl_3_cout), .count(Count), .load(lOAD), .in_4(in_3[15:12]), .clk(CLK_out), .clr(CLR),
    .out_7(out_5[15:12]), .Cout(n4bit_cpl_4_cout));
  _4bit_CPL u_4bit_cpl_5 (
    .Cin(n4bit_cpl_4_cout), .count(Count), .load(lOAD), .in_4(in_3[19:16]), .clk(CLK_out), .clr(CLR),
    .out_7(out_5[19:16]), .Cout(n4bit_cpl_5_cout));
  _2bit_CPL u_2bit_cpl_1 (
    .Cin(n4bit_cpl_5_cout), .count(Count), .LOAD(lOAD), .in_4(in_3[21:20]), .CLR(CLR), .CLK(CLK_out),
    .out_7(out_5[21:20]));
  // Probe on out_5

  // Notes on the sheet:
  //   2207035
  //   22 bit CPL
endmodule

// 22 bit MBR
module _22bit_MBR (
  input  lOAD,
  input  Count,
  input  [21:0] in_3,
  input  Clk,
  input  CLR,
  output [21:0] out_6
);

  wire n4bit_cpl_1_cout, n4bit_cpl_2_cout, n4bit_cpl_3_cout, n4bit_cpl_4_cout, n4bit_cpl_5_cout;

  _4bit_CPL u_4bit_cpl_1 (
    .Cin(Count), .count(Count), .load(lOAD), .in_4(in_3[3:0]), .clk(Clk), .clr(CLR), .out_7(out_6[3:0]),
    .Cout(n4bit_cpl_1_cout));
  _4bit_CPL u_4bit_cpl_2 (
    .Cin(n4bit_cpl_1_cout), .count(Count), .load(lOAD), .in_4(in_3[7:4]), .clk(Clk), .clr(CLR),
    .out_7(out_6[7:4]), .Cout(n4bit_cpl_2_cout));
  _4bit_CPL u_4bit_cpl_3 (
    .Cin(n4bit_cpl_2_cout), .count(Count), .load(lOAD), .in_4(in_3[11:8]), .clk(Clk), .clr(CLR),
    .out_7(out_6[11:8]), .Cout(n4bit_cpl_3_cout));
  _4bit_CPL u_4bit_cpl_4 (
    .Cin(n4bit_cpl_3_cout), .count(Count), .load(lOAD), .in_4(in_3[15:12]), .clk(Clk), .clr(CLR),
    .out_7(out_6[15:12]), .Cout(n4bit_cpl_4_cout));
  _4bit_CPL u_4bit_cpl_5 (
    .Cin(n4bit_cpl_4_cout), .count(Count), .load(lOAD), .in_4(in_3[19:16]), .clk(Clk), .clr(CLR),
    .out_7(out_6[19:16]), .Cout(n4bit_cpl_5_cout));
  _2bit_CPL u_2bit_cpl_1 (
    .Cin(n4bit_cpl_5_cout), .count(Count), .LOAD(lOAD), .in_4(in_3[21:20]), .CLR(CLR), .CLK(Clk),
    .out_7(out_6[21:20]));
  // Probe on out_6

  // Notes on the sheet:
  //   2207035
  //   22 bit MBR
endmodule

// IR
module _4bit_IR (
  input  LOAD,
  input  [3:0] in_2,
  input  Clk,
  input  CLR,
  output [3:0] out_5
);

  wire and_1_out, and_2_out, and_3_out, and_4_out, and_5_out, and_6_out, and_7_out, and_8_out, not_1_out,
       not_2_out, not_3_out, not_4_out;

  not not_1 (not_1_out, in_2[0]);
  not not_2 (not_2_out, in_2[1]);
  not not_3 (not_3_out, in_2[2]);
  not not_4 (not_4_out, in_2[3]);
  and and_1 (and_1_out, in_2[0], LOAD);
  and and_2 (and_2_out, not_1_out, LOAD);
  and and_3 (and_3_out, in_2[1], LOAD);
  and and_4 (and_4_out, not_2_out, LOAD);
  and and_5 (and_5_out, in_2[2], LOAD);
  and and_6 (and_6_out, not_3_out, LOAD);
  and and_7 (and_7_out, in_2[3], LOAD);
  and and_8 (and_8_out, not_4_out, LOAD);
  J_K_Flip_Flop j_k_ff_1 (.J(and_1_out), .clk(Clk), .K(and_2_out), .Q(out_5[0]), .reset(CLR));  // open: Qn, preset, en
  J_K_Flip_Flop j_k_ff_2 (.J(and_3_out), .clk(Clk), .K(and_4_out), .Q(out_5[1]), .reset(CLR));  // open: Qn, preset, en
  J_K_Flip_Flop j_k_ff_3 (.J(and_5_out), .clk(Clk), .K(and_6_out), .Q(out_5[2]), .reset(CLR));  // open: Qn, preset, en
  J_K_Flip_Flop j_k_ff_4 (.J(and_7_out), .clk(Clk), .K(and_8_out), .Q(out_5[3]), .reset(CLR));  // open: Qn, preset, en

  // Notes on the sheet:
  //   2207035
  //   4 bit IR
endmodule

// PC
module _5bit_PC (
  input  lOAD,
  input  Count,
  input  [4:0] in_3,
  input  Clk,
  input  CLR,
  output [4:0] out_6
);

  wire n4bit_cpl_1_cout;

  _4bit_CPL u_4bit_cpl_1 (
    .Cin(Count), .count(Count), .load(lOAD), .in_4(in_3[3:0]), .clk(Clk), .clr(CLR), .out_7(out_6[3:0]),
    .Cout(n4bit_cpl_1_cout));
  _1bit_CPL u_1bit_cpl_1 (
    .Cin(n4bit_cpl_1_cout), .count(Count), .LOAD(lOAD), .in_4(in_3[4]), .CLR(CLR), .CLK(Clk), .out_7(out_6[4]));
  // Probe on out_6

  // Notes on the sheet:
  //   2207035
  //   5 bit PC
endmodule

// CPL
module _1bit_CPL (
  input  Cin,
  input  count,
  input  LOAD,
  input  in_4,
  input  CLR,
  input  CLK,
  output out_7
);

  wire and_1_out, and_2_out, and_3_out, and_4_out, not_1_out, not_2_out, or_1_out, or_2_out;

  and and_1 (and_1_out, count, not_1_out);
  not not_1 (not_1_out, LOAD);
  not not_2 (not_2_out, in_4);
  and and_2 (and_2_out, LOAD, in_4);
  and and_3 (and_3_out, LOAD, not_2_out);
  and and_4 (and_4_out, and_1_out, Cin);
  or or_1 (or_1_out, and_2_out, and_4_out);
  or or_2 (or_2_out, and_4_out, and_3_out);
  J_K_Flip_Flop j_k_ff_1 (.J(or_1_out), .clk(CLK), .K(or_2_out), .Q(out_7), .reset(CLR));  // open: Qn, preset, en

  // Notes on the sheet:
  //   2207035
  //   1 bit CPL
endmodule

// MAR
module _5bit_MAR (
  input  lOAD,
  input  Count,
  input  [4:0] in_3,
  input  Clk,
  input  CLR,
  output [4:0] out_6
);

  wire n4bit_cpl_1_cout;

  _4bit_CPL u_4bit_cpl_1 (
    .Cin(Count), .count(Count), .load(lOAD), .in_4(in_3[3:0]), .clk(Clk), .clr(CLR), .out_7(out_6[3:0]),
    .Cout(n4bit_cpl_1_cout));
  _1bit_CPL u_1bit_cpl_1 (
    .Cin(n4bit_cpl_1_cout), .count(Count), .LOAD(lOAD), .in_4(in_3[4]), .CLR(CLR), .CLK(Clk), .out_7(out_6[4]));
  // Probe on out_6

  // Notes on the sheet:
  //   2207035
  //   5 bit MAR
endmodule

// ACC
module _22bit_ACC (
  input  load,
  input  [21:0] in_2,
  input  Clk,
  input  Clr,
  output [21:0] out_5
);

  _4bit_PLR u_4bit_plr_1 (.in_2(in_2[3:0]), .CLK(Clk), .CLR(Clr), .LOAD(load), .out_5(out_5[3:0]));
  _4bit_PLR u_4bit_plr_2 (.in_2(in_2[7:4]), .CLK(Clk), .CLR(Clr), .LOAD(load), .out_5(out_5[7:4]));
  _4bit_PLR u_4bit_plr_3 (.in_2(in_2[11:8]), .CLK(Clk), .CLR(Clr), .LOAD(load), .out_5(out_5[11:8]));
  _4bit_PLR u_4bit_plr_4 (.in_2(in_2[15:12]), .CLK(Clk), .CLR(Clr), .LOAD(load), .out_5(out_5[15:12]));
  _4bit_PLR u_4bit_plr_5 (.in_2(in_2[19:16]), .CLK(Clk), .CLR(Clr), .LOAD(load), .out_5(out_5[19:16]));
  _2bit_PLR u_2bit_plr_1 (.in_2(in_2[21:20]), .CLK(Clk), .CLR(Clr), .LOAD(load), .out_5(out_5[21:20]));

  // Notes on the sheet:
  //   2207035
  //   22 bit ACC
endmodule

// CU
module _22bit_Control_Unit (
  input  [21:0] Data_In,
  input  Reset,
  input  Clk,
  output Load,
  output OUT_CLOCK,
  output [21:0] Data_out,
  output [4:0] MAR_OUT,
  output Store
);

  wire _3, _4, _5, ACCtoMBR, ADD, ALU_ADD, ALU_AND, ALU_SUB, AND, and_12_out, BSB, change_to_0, change_to_1,
       CMP, CNG_OPCODE, Fetch, FLAGStoREG, HALT, ISZ, JC, JMP, JN, JO, JZ, LOAD_t, MBR_INC, MBR_Zero,
       MBRtoACC, MBRtoIR, MBRtoMAR, MBRtoMEM_1, MBRtoMEM_2, MBRtoMEM_3, MBRtoPC_1, MBRtoPC_2, MBRtoPC_3,
       MBRtoPC_4, MBRtoPC_5, MEMtoMBR_1, MEMtoMBR_2, n22bit_zero_check_1_output__zero_0, not_1_out,
       not_2_out, not_3_out, not_5_out, or_1_out, or_2_out, or_3_out, or_4_out, or_7_out, or_8_out, or_9_out,
       or_10_out, or_11_out, PC_INC_2, PCtoMAR, STO, t0, t1, t2, t3;
  wire [1:0] counter_1_q, n2bit_alu_select_1_out_4;
  wire [3:0] bit_extender_1_out, FLAG_IN, FLAG_OUT, IR_OUT;
  wire [4:0] Address, multiplexer_1_out, multiplexer_4_out;
  wire [19:0] NewMBR;
  wire [21:0] ACC_IN, ACC_OUT, multiplexer_3_out, multiplexer_5_out, n22bit_alu_1_output;
  wire [21:5] MBR_OUT;

  Counter #(.width(2), .max('h3)) counter_1 (
    .Q(counter_1_q), .clk(OUT_CLOCK), .clr(Reset));  // open: load, D, count, carry
  Decoder #(.select(4), .enable("false")) decoder_1 (
    .out0(AND), .out1(ADD), .out2(STO), .out3(ISZ), .out4(BSB), .out5(JMP), .out6(LOAD_t), .out7(HALT),
    .out8(CMP), .out9(JZ), .out10(JN), .out11(JC), .out12(JO), .out13(_3), .out14(_4), .out15(_5),
    .sel(IR_OUT));
  not not_1 (not_1_out, Fetch);
  not not_2 (not_2_out, Fetch);
  not not_3 (not_3_out, Fetch);
  Decoder #(.select(2), .enable("false")) decoder_2 (.out0(t0), .out1(t1), .out2(t2), .out3(t3), .sel(counter_1_q));
  and and_1 (PCtoMAR, not_1_out, t0);
  and and_2 (MEMtoMBR_1, not_2_out, t1);
  and and_3 (MBRtoIR, not_3_out, t2);
  and and_4 (ALU_AND, Fetch, t2, AND);
  and and_5 (ALU_ADD, Fetch, t2, ADD);
  and and_6 (ACCtoMBR, Fetch, t2, STO);
  and and_7 (MBRtoMEM_3, Fetch, t3, STO);
  and and_8 (ALU_SUB, ~Fetch, t1, CMP);  // AND_Gate
  and and_9 (FLAGStoREG, ~Fetch, t1, CMP);  // AND_Gate
  and and_10 (OUT_CLOCK, Clk, ~HALT);  // AND_Gate
  or or_1 (or_1_out, MBRtoPC_1, MBRtoPC_2, MBRtoPC_3, MBRtoPC_4, MBRtoPC_5);
  Multiplexer #(.width(5), .enable("false")) multiplexer_1 (
    .in0(MAR_OUT), .in1(Address), .out(multiplexer_1_out), .sel(or_1_out));
  or or_2 (or_2_out, MEMtoMBR_1, PC_INC_2, MBRtoMEM_1);
  _2bit_ALU_Select u_2bit_alu_select_1 (.ADD(ALU_ADD), .SUB(ALU_SUB), .AND(ALU_AND), .out_4(n2bit_alu_select_1_out_4));
  _22bit_zero_check u_22bit_zero_check_1 (
    .Input({MBR_OUT, Address}), .output__zero_0(n22bit_zero_check_1_output__zero_0));
  and and_11 (change_to_0, Fetch, t3);
  or or_3 (or_3_out, ALU_ADD, ALU_SUB, ALU_AND);
  // Probe on n2bit_alu_select_1_out_4
  _22bit_ALU u_22bit_alu_1 (
    .Control(n2bit_alu_select_1_out_4), .A(ACC_OUT), .B({MBR_OUT, Address}), .\output (n22bit_alu_1_output),
    .Negative_Zero_CarryOut_Overflow(FLAG_IN));
  Register #(.width(4)) register_1 (.D(FLAG_IN), .en(FLAGStoREG), .Q(FLAG_OUT), .clk(OUT_CLOCK), .clr(Reset));
  not not_4 (MBR_Zero, n22bit_zero_check_1_output__zero_0);
  or or_4 (or_4_out, CNG_OPCODE, or_1_out);
  Multiplexer #(.width(22), .enable("false")) multiplexer_2 (
    .in0(ACC_OUT), .in1(n22bit_alu_1_output), .out(ACC_IN), .sel(and_12_out));
  and and_12 (and_12_out, or_3_out, t2);
  J_K_Flip_Flop j_k_ff_1 (.J(change_to_1), .clk(OUT_CLOCK), .K(change_to_0), .Q(Fetch));  // open: Qn, preset, en, reset
  _5bit_PC u_5bit_pc_1 (
    .Count(or_2_out), .in_3(multiplexer_1_out), .Clk(OUT_CLOCK), .CLR(Reset), .lOAD(or_4_out),
    .out_6(NewMBR[4:0]));
  and and_13 (MBRtoPC_1, JMP, t3);
  and and_14 (MBRtoMAR, Fetch, t0);
  and and_15 (MBR_INC, Fetch, t2, ISZ);
  and and_16 (MBRtoMEM_2, Fetch, t3, ISZ);
  and and_17 (PC_INC_2, Fetch, t3, MBR_Zero, ISZ);
  and and_18 (MBRtoPC_2, FLAG_OUT[2], ~Fetch, JZ, t3);  // AND_Gate
  and and_19 (MBRtoPC_3, FLAG_OUT[3], ~Fetch, JN, t3);  // AND_Gate
  Multiplexer #(.select(2), .width(22), .enable("false")) multiplexer_3 (
    .in0(Data_In), .in1({2'b00, NewMBR[19:16], {11{1'b0}}, NewMBR[4:0]}), .in2(ACC_OUT),
    .out(multiplexer_3_out), .sel({ACCtoMBR, CNG_OPCODE}));  // open: in3
  or or_5 (Load, MEMtoMBR_1, MEMtoMBR_2);
  Multiplexer #(.width(5), .enable("false")) multiplexer_4 (
    .in0(NewMBR[4:0]), .in1(Address), .out(multiplexer_4_out), .sel(MBRtoMAR));
  Multiplexer #(.width(22), .enable("false")) multiplexer_5 (
    .in0(ACC_IN), .in1({MBR_OUT, Address}), .out(multiplexer_5_out), .sel(MBRtoACC));
  or or_6 (Store, MBRtoMEM_1, MBRtoMEM_2, MBRtoMEM_3);
  // Probe on bit_extender_1_out
  assign bit_extender_1_out = {{3{CNG_OPCODE}}, CNG_OPCODE};  // Bit_Extender bit_extender_1
  // Probe on 4'b0101
  or or_7 (or_7_out, Load, ACCtoMBR, CNG_OPCODE);
  or or_8 (or_8_out, ALU_ADD, ALU_AND, MBRtoACC);
  Multiplexer #(.width(22), .enable("false")) multiplexer_6 (
    .in0(Data_In), .in1({MBR_OUT, Address}), .out(Data_out), .sel(Store));
  assign NewMBR[19:16] = bit_extender_1_out & 4'b0101;  // AND_Gate and_20, 4 bits wide
  // Probe on NewMBR[19:16]
  _22bit_MBR u_22bit_mbr_1 (
    .Count(MBR_INC), .in_3(multiplexer_3_out), .Clk(OUT_CLOCK), .CLR(Reset), .lOAD(or_7_out),
    .out_6({MBR_OUT, Address}));
  // Probe on multiplexer_4_out
  _4bit_IR u_4bit_ir_1 (.in_2(MBR_OUT[19:16]), .Clk(OUT_CLOCK), .CLR(Reset), .LOAD(MBRtoIR), .out_5(IR_OUT));
  _22bit_ACC u_22bit_acc_1 (.in_2(multiplexer_5_out), .Clk(OUT_CLOCK), .Clr(Reset), .load(or_8_out), .out_5(ACC_OUT));
  or or_9 (or_9_out, AND, ADD, ISZ, LOAD_t, CMP, JZ, JN, JC, JO, _3, _4, _5);
  or or_10 (or_10_out, PCtoMAR, MBRtoMAR);
  and and_21 (MEMtoMBR_2, Fetch, t1, or_9_out);
  and and_22 (CNG_OPCODE, Fetch, t2, BSB);
  and and_23 (MBRtoMEM_1, Fetch, t3, BSB);
  and and_24 (MBRtoACC, Fetch, t2, LOAD_t);
  and and_25 (MBRtoPC_4, FLAG_OUT[1], ~Fetch, JC, t3);  // AND_Gate
  and and_26 (MBRtoPC_5, FLAG_OUT[0], ~Fetch, JO, t3);  // AND_Gate
  _5bit_MAR u_5bit_mar_1 (
    .Count(1'b0), .in_3(multiplexer_4_out), .Clk(OUT_CLOCK), .CLR(Reset), .lOAD(or_10_out), .out_6(MAR_OUT));
  not not_5 (not_5_out, Fetch);
  or or_11 (or_11_out, AND, ADD, STO, ISZ, BSB, LOAD_t, HALT, CMP, JZ, JN, JC, JO, _3, _4, _5);
  and and_27 (change_to_1, not_5_out, t3, or_11_out);

  // Other names for the same wires on the sheet: MARtoPC = CNG_OPCODE; PCtoMBR = CNG_OPCODE; Clk_t = OUT_CLOCK;
  //   isOverflow = FLAG_OUT[0]; isCarry = FLAG_OUT[1]; isZero = FLAG_OUT[2]; isNeg = FLAG_OUT[3];
  //   MBR_OUT[4:0] = Address; Opcode[3:0] = MBR_OUT[19:16]; PC_out[4:0] = NewMBR[4:0]; PC_INC_1 = MEMtoMBR_1;
  //   PC_INC_3 = MBRtoMEM_1

  // Notes on the sheet:
  //   2207035
  //   22 bit Control Unit
endmodule

// ALU OP
module _2bit_ALU_Select (
  input  ADD,
  input  SUB,
  input  AND,
  output [1:0] out_4
);

  wire and_1_out, and_2_out, and_3_out, not_1_out, not_2_out, not_3_out;

  not not_1 (not_1_out, ADD);
  not not_2 (not_2_out, SUB);
  not not_3 (not_3_out, AND);
  and and_1 (and_1_out, ADD, not_2_out, not_3_out);
  and and_2 (and_2_out, not_1_out, SUB, not_3_out);
  and and_3 (and_3_out, not_1_out, not_2_out, AND);
  or or_1 (out_4[1], and_1_out, and_2_out);
  or or_2 (out_4[0], and_2_out, and_3_out);

  // Notes on the sheet:
  //   2207035
  //   2 bit ALU Select
endmodule

module The_22bit_Computer (
  input  Reset
);

  wire Clk_out, n22bit_control_unit_1_load, n22bit_control_unit_1_out_clock, n22bit_control_unit_1_store;
  wire [4:0] n22bit_control_unit_1_mar_out;
  wire [21:0] n22bit_control_unit_1_data_out, ram_1_data;

  Clock Clk (.out(Clk_out));
  _22bit_Control_Unit u_22bit_control_unit_1 (
    .Data_In(ram_1_data), .Reset(Reset), .Clk(Clk_out), .Data_out(n22bit_control_unit_1_data_out),
    .Load(n22bit_control_unit_1_load), .OUT_CLOCK(n22bit_control_unit_1_out_clock),
    .MAR_OUT(n22bit_control_unit_1_mar_out), .Store(n22bit_control_unit_1_store));
  RAM #(.addrWidth(5), .dataWidth(22), .bus("separate")) ram_1 (
    .addr(n22bit_control_unit_1_mar_out), .din(n22bit_control_unit_1_data_out), .data(ram_1_data),
    .str(n22bit_control_unit_1_store), .clk(n22bit_control_unit_1_out_clock), .ld(n22bit_control_unit_1_load));  // open: sel, clr

  // Notes on the sheet:
  //   2207035
  //   The 22 bit Computer
  //   32 words RAM
endmodule
